// Logisim project HW#02-4bit register.circ as structural Verilog: 5 circuits, main circuit SR Latch
module SR_Latch (
  input  R,
  input  S,
  input  nS,
  input  nR,
  output Q,
  output nQ,
  output Q_2,
  output nQ_2
);

  nor nor_1 (Q, R, nQ);
  nor nor_2 (nQ, Q, S);
  nand nand_1 (Q_2, nS, nQ_2);
  nand nand_2 (nQ_2, Q_2, nR);
endmodule

module gated_SR_Latch (
  input  R,
  input  E,
  input  S,
  output Q,
  output nQ
);

  wire and_1_out, and_2_out;

  and and_1 (and_1_out, R, E);
  and and_2 (and_2_out, E, S);
  nor nor_1 (Q, and_1_out, nQ);
  nor nor_2 (nQ, Q, and_2_out);
endmodule

// D latch
module gated_D_Latch (
  input  Crear,
  input  D,
  input  E,
  input  Preset,
  output Q,
  output nQ
);

  wire and_1_out, and_2_out, not_1_out;

  not not_1 (not_1_out, D);
  and and_1 (and_1_out, not_1_out, E);
  and and_2 (and_2_out, E, D);
  nor nor_1 (Q, Crear, and_1_out, nQ);
  nor nor_2 (nQ, Q, and_2_out, Preset);
endmodule

// D FF
module D_flip_flop (
  input  Crear,
  input  D,
  input  Ck,
  input  Preset,
  output Q,
  output nQ
);

  wire gated_d_latch_1_q, not_1_out;

  gated_D_Latch gated_d_latch_1 (.D(D), .E(not_1_out), .Q(gated_d_latch_1_q), .Crear(1'b0), .Preset(1'b0));  // open: nQ
  not not_1 (not_1_out, Ck);
  gated_D_Latch gated_d_latch_2 (.D(gated_d_latch_1_q), .E(Ck), .Q(Q), .nQ(nQ), .Crear(Crear), .Preset(Preset));
endmodule

module _4bit_register (
  input  [3:0] D,
  input  [3:0] Preset,
  input  Crear,
  input  Ck,
  output [3:0] Q
);

  D_flip_flop d_flip_flop_1 (.D(D[0]), .Ck(Ck), .Q(Q[0]), .Crear(Crear), .Preset(Preset[0]));  // open: nQ
  D_flip_flop d_flip_flop_2 (.D(D[1]), .Ck(Ck), .Q(Q[1]), .Crear(Crear), .Preset(Preset[1]));  // open: nQ
  D_flip_flop d_flip_flop_3 (.D(D[2]), .Ck(Ck), .Q(Q[2]), .Crear(Crear), .Preset(Preset[2]));  // open: nQ
  D_flip_flop d_flip_flop_4 (.D(D[3]), .Ck(Ck), .Q(Q[3]), .Crear(Crear), .Preset(Preset[3]));  // open: nQ
endmodule
