// Logisim project HW#03-8bit LU and shifter.circ as structural Verilog: 7 circuits, main circuit 2x1 MUX
module _2x1_MUX (
  input  S,
  input  l0,
  input  l1,
  output O
);

  wire and_1_out, and_2_out, not_1_out;

  not not_1 (not_1_out, S);
  and and_1 (and_1_out, not_1_out, l0);
  and and_2 (and_2_out, S, l1);
  or or_1 (O, and_1_out, and_2_out);
endmodule

// 4x1 mux
module _4x1_MUX (
  input  S1,
  input  S0,
  input  l0,
  input  l1,
  input  l2,
  input  l3,
  output O
);

  wire and_1_out, and_2_out, and_3_out, and_4_out, not_1_out, not_2_out;

  not not_1 (not_1_out, S1);
  not not_2 (not_2_out, S0);
  and and_1 (and_1_out, not_2_out, not_1_out, l0);
  and and_2 (and_2_out, S0, not_1_out, l1);
  and and_3 (and_3_out, not_2_out, S1, l2);
  and and_4 (and_4_out, S0, S1, l3);
  or or_1 (O, and_1_out, and_2_out, and_3_out, and_4_out);
endmodule

// 1bit LU
module _1bit_Logical_unit (
  input  A,
  input  B,
  input  S1,
  input  S0,
  output out_5
);

  wire and_1_out, not_1_out, or_1_out, xor_1_out;

  not not_1 (not_1_out, A);
  and and_1 (and_1_out, A, B);
  or or_1 (or_1_out, A, B);
  xor xor_1 (xor_1_out, A, B);
  _4x1_MUX u_4x1_mux_1 (.S1(S1), .S0(S0), .l0(and_1_out), .l1(or_1_out), .l2(xor_1_out), .l3(not_1_out), .O(out_5));
endmodule

module _4bit_LU (
  input  [3:0] A,
  input  [3:0] B,
  input  S1,
  input  S0,
  output [3:0] F
);

  _1bit_Logical_unit u_1bit_logical_unit_1 (.A(A[0]), .B(B[0]), .S1(S1), .S0(S0), .out_5(F[0]));
  _1bit_Logical_unit u_1bit_logical_unit_2 (.A(A[1]), .B(B[1]), .S1(S1), .S0(S0), .out_5(F[1]));
  _1bit_Logical_unit u_1bit_logical_unit_3 (.A(A[2]), .B(B[2]), .S1(S1), .S0(S0), .out_5(F[2]));
  _1bit_Logical_unit u_1bit_logical_unit_4 (.A(A[3]), .B(B[3]), .S1(S1), .S0(S0), .out_5(F[3]));
endmodule

// 4 shift
module _4bit_shifter (
  input  SRin,
  input  [3:0] l,
  input  SLin,
  input  S1,
  input  S0,
  output [3:0] O
);

  _4x1_MUX u_4x1_mux_1 (.S1(S1), .S0(S0), .l0(l[0]), .l1(l[1]), .l2(SRin), .l3(1'b0), .O(O[0]));
  _4x1_MUX u_4x1_mux_2 (.S1(S1), .S0(S0), .l0(l[1]), .l1(l[2]), .l2(l[0]), .l3(1'b0), .O(O[1]));
  _4x1_MUX u_4x1_mux_3 (.S1(S1), .S0(S0), .l0(l[2]), .l1(l[3]), .l2(l[1]), .l3(1'b0), .O(O[2]));
  _4x1_MUX u_4x1_mux_4 (.S1(S1), .S0(S0), .l0(l[3]), .l1(SLin), .l2(l[2]), .l3(1'b0), .O(O[3]));
endmodule

module _8bit_LU (
  input  [7:0] A,
  input  [7:0] B,
  input  S1,
  input  S0,
  output [7:0] F
);

  _4bit_LU u_4bit_lu_1 (.A(A[3:0]), .B(B[3:0]), .S1(S1), .S0(S0), .F(F[3:0]));
  _4bit_LU u_4bit_lu_2 (.A(A[7:4]), .B(B[7:4]), .S1(S1), .S0(S0), .F(F[7:4]));
endmodule

module _8bit_shifter (
  input  SRin,
  input  [7:0] l,
  input  SLin,
  input  S1,
  input  S0,
  output [7:0] O
);

  _4bit_shifter u_4bit_shifter_1 (.SRin(SRin), .l(l[3:0]), .SLin(l[4]), .S1(S1), .S0(S0), .O(O[3:0]));
  _4bit_shifter u_4bit_shifter_2 (.SRin(l[3]), .l(l[7:4]), .SLin(SLin), .S1(S1), .S0(S0), .O(O[7:4]));
endmodule
