// Logisim project HW#04-8bit AU and ALU.circ as structural Verilog
module _2x1_MUX (
  input  S,
  input  l0,
  input  l1,
  output O
);

  wire and_1_out, and_2_out, not_1_out;

  not not_1 (not_1_out, S);
  and and_1 (and_1_out, not_1_out, l0);
  and and_2 (and_2_out, S, l1);
  or or_1 (O, and_1_out, and_2_out);
endmodule

// 4x1 mux
module _4x1_MUX (
  input  S1,
  input  S0,
  input  l0,
  input  l1,
  input  l2,
  input  l3,
  output O
);

  wire and_1_out, and_2_out, and_3_out, and_4_out, not_1_out, not_2_out;

  not not_1 (not_1_out, S1);
  not not_2 (not_2_out, S0);
  and and_1 (and_1_out, not_2_out, not_1_out, l0);
  and and_2 (and_2_out, S0, not_1_out, l1);
  and and_3 (and_3_out, not_2_out, S1, l2);
  and and_4 (and_4_out, S0, S1, l3);
  or or_1 (O, and_1_out, and_2_out, and_3_out, and_4_out);
endmodule

// 1bit LU
module _1bit_Logical_unit (
  input  A,
  input  B,
  input  S1,
  input  S0,
  output out_5
);

  wire and_1_out, not_1_out, or_1_out, xor_1_out;

  not not_1 (not_1_out, A);
  and and_1 (and_1_out, A, B);
  or or_1 (or_1_out, A, B);
  xor xor_1 (xor_1_out, A, B);
  _4x1_MUX u_4x1_mux_1 (.S1(S1), .S0(S0), .l0(and_1_out), .l1(or_1_out), .l2(xor_1_out), .l3(not_1_out), .O(out_5));
endmodule

module _4bit_LU (
  input  [3:0] A,
  input  [3:0] B,
  input  S1,
  input  S0,
  output [3:0] F
);

  _1bit_Logical_unit u_1bit_logical_unit_1 (.A(A[0]), .B(B[0]), .S1(S1), .S0(S0), .out_5(F[0]));
  _1bit_Logical_unit u_1bit_logical_unit_2 (.A(A[1]), .B(B[1]), .S1(S1), .S0(S0), .out_5(F[1]));
  _1bit_Logical_unit u_1bit_logical_unit_3 (.A(A[2]), .B(B[2]), .S1(S1), .S0(S0), .out_5(F[2]));
  _1bit_Logical_unit u_1bit_logical_unit_4 (.A(A[3]), .B(B[3]), .S1(S1), .S0(S0), .out_5(F[3]));
endmodule

// 4 shift
module _4bit_shifter (
  input  SRin,
  input  [3:0] l,
  input  SLin,
  input  S1,
  input  S0,
  output [3:0] O
);

  _4x1_MUX u_4x1_mux_1 (.S1(S1), .S0(S0), .l0(l[0]), .l1(l[1]), .l2(SRin), .l3(1'b0), .O(O[0]));
  _4x1_MUX u_4x1_mux_2 (.S1(S1), .S0(S0), .l0(l[1]), .l1(l[2]), .l2(l[0]), .l3(1'b0), .O(O[1]));
  _4x1_MUX u_4x1_mux_3 (.S1(S1), .S0(S0), .l0(l[2]), .l1(l[3]), .l2(l[1]), .l3(1'b0), .O(O[2]));
  _4x1_MUX u_4x1_mux_4 (.S1(S1), .S0(S0), .l0(l[3]), .l1(SLin), .l2(l[2]), .l3(1'b0), .O(O[3]));
endmodule

module _8bit_LU (
  input  [7:0] A,
  input  [7:0] B,
  input  S1,
  input  S0,
  output [7:0] F
);

  _4bit_LU u_4bit_lu_1 (.A(A[3:0]), .B(B[3:0]), .S1(S1), .S0(S0), .F(F[3:0]));
  _4bit_LU u_4bit_lu_2 (.A(A[7:4]), .B(B[7:4]), .S1(S1), .S0(S0), .F(F[7:4]));
endmodule

// 8 shift
module _8bit_shifter (
  input  SRin,
  input  [7:0] l,
  input  SLin,
  input  S1,
  input  S0,
  output [7:0] O
);

  _4bit_shifter u_4bit_shifter_1 (.SRin(SRin), .SLin(l[4]), .S1(S1), .S0(S0), .O(O[3:0]), .l(l[3:0]));
  _4bit_shifter u_4bit_shifter_2 (.SRin(l[3]), .SLin(SLin), .S1(S1), .S0(S0), .O(O[7:4]), .l(l[7:4]));
endmodule

// FA
module Full_Adder (
  input  A,
  input  B,
  input  Ci,
  output S,
  output Co
);

  wire and_1_out, and_2_out, and_3_out, and_4_out, and_5_out, and_6_out, and_7_out, not_1_out, not_2_out,
       not_3_out, not_4_out, not_5_out, not_6_out;

  not not_1 (not_1_out, A);
  not not_2 (not_2_out, B);
  not not_3 (not_3_out, A);
  not not_4 (not_4_out, Ci);
  not not_5 (not_5_out, B);
  not not_6 (not_6_out, Ci);
  and and_1 (and_1_out, B, Ci);
  and and_2 (and_2_out, A, Ci);
  and and_3 (and_3_out, A, B);
  and and_4 (and_4_out, not_1_out, not_2_out, Ci);
  and and_5 (and_5_out, not_3_out, B, not_4_out);
  and and_6 (and_6_out, A, not_5_out, not_6_out);
  and and_7 (and_7_out, A, B, Ci);
  or or_1 (Co, and_1_out, and_2_out, and_3_out);
  or or_2 (S, and_4_out, and_5_out, and_6_out, and_7_out);
endmodule

module _1bit_AU (
  input  Ci,
  input  A,
  input  B,
  input  S1,
  input  S0,
  output F,
  output Co
);

  wire n4x1_mux_1_o, not_1_out;

  _4x1_MUX u_4x1_mux_1 (.S1(S1), .S0(S0), .l0(1'b0), .l1(B), .l2(not_1_out), .l3(1'b1), .O(n4x1_mux_1_o));
  not not_1 (not_1_out, B);
  Full_Adder full_adder_1 (.A(A), .B(n4x1_mux_1_o), .Ci(Ci), .S(F), .Co(Co));
endmodule

module _4bit_AU (
  input  Ci,
  input  [3:0] A,
  input  [3:0] B,
  input  S1,
  input  S0,
  output [3:0] F,
  output V,
  output Co
);

  wire n1bit_au_1_co, n1bit_au_2_co, n1bit_au_3_co;

  _1bit_AU u_1bit_au_1 (.Ci(Ci), .A(A[0]), .B(B[0]), .S1(S1), .S0(S0), .F(F[0]), .Co(n1bit_au_1_co));
  _1bit_AU u_1bit_au_2 (.Ci(n1bit_au_1_co), .A(A[1]), .B(B[1]), .S1(S1), .S0(S0), .F(F[1]), .Co(n1bit_au_2_co));
  _1bit_AU u_1bit_au_3 (.Ci(n1bit_au_2_co), .A(A[2]), .B(B[2]), .S1(S1), .S0(S0), .F(F[2]), .Co(n1bit_au_3_co));
  _1bit_AU u_1bit_au_4 (.Ci(n1bit_au_3_co), .A(A[3]), .B(B[3]), .S1(S1), .S0(S0), .F(F[3]), .Co(Co));
  xor xor_1 (V, n1bit_au_3_co, Co);
endmodule

// 4 2x1
module _4bit_2x1_MUX (
  input  [3:0] A,
  input  [3:0] B,
  input  S,
  output [3:0] O
);

  _2x1_MUX u_2x1_mux_1 (.S(S), .l0(A[0]), .l1(B[0]), .O(O[0]));
  _2x1_MUX u_2x1_mux_2 (.S(S), .l0(A[1]), .l1(B[1]), .O(O[1]));
  _2x1_MUX u_2x1_mux_3 (.S(S), .l0(A[2]), .l1(B[2]), .O(O[2]));
  _2x1_MUX u_2x1_mux_4 (.S(S), .l0(A[3]), .l1(B[3]), .O(O[3]));
endmodule

module _4bit_ALU (
  input  Ci,
  input  [3:0] A,
  input  [3:0] B,
  input  S2,
  input  H1,
  input  S1,
  input  H0,
  input  S0,
  output V,
  output Co,
  output Z,
  output S,
  output [3:0] F
);

  wire [3:0] n4bit_2x1_mux_1_o, n4bit_au_1_f, n4bit_lu_1_f;

  _4bit_AU u_4bit_au_1 (.Ci(Ci), .A(A), .B(B), .S1(S1), .S0(S0), .F(n4bit_au_1_f), .V(V), .Co(Co));
  _4bit_LU u_4bit_lu_1 (.A(A), .B(B), .S1(S1), .S0(S0), .F(n4bit_lu_1_f));
  _4bit_2x1_MUX u_4bit_2x1_mux_1 (.A(n4bit_au_1_f), .B(n4bit_lu_1_f), .S(S2), .O(n4bit_2x1_mux_1_o));
  _4bit_shifter u_4bit_shifter_1 (.SRin(1'b0), .SLin(1'b0), .S1(H1), .S0(H0), .O(F), .l(n4bit_2x1_mux_1_o));
  nor nor_1 (Z, F[0], F[1], F[2], F[3]);

  assign S = F[3];
endmodule

module _8bit_AU (
  input  Ci,
  input  [7:0] A,
  input  [7:0] B,
  input  S1,
  input  S0,
  output [7:0] F,
  output V,
  output Co
);

  wire n1bit_au_1_co, n1bit_au_2_co, n1bit_au_3_co, n1bit_au_4_co, n1bit_au_5_co, n1bit_au_6_co,
       n1bit_au_7_co;

  _1bit_AU u_1bit_au_1 (.Ci(Ci), .A(A[0]), .B(B[0]), .S1(S1), .S0(S0), .F(F[0]), .Co(n1bit_au_1_co));
  _1bit_AU u_1bit_au_2 (.Ci(n1bit_au_1_co), .A(A[1]), .B(B[1]), .S1(S1), .S0(S0), .F(F[1]), .Co(n1bit_au_2_co));
  _1bit_AU u_1bit_au_3 (.Ci(n1bit_au_2_co), .A(A[2]), .B(B[2]), .S1(S1), .S0(S0), .F(F[2]), .Co(n1bit_au_3_co));
  _1bit_AU u_1bit_au_4 (.Ci(n1bit_au_3_co), .A(A[3]), .B(B[3]), .S1(S1), .S0(S0), .F(F[3]), .Co(n1bit_au_4_co));
  _1bit_AU u_1bit_au_5 (.Ci(n1bit_au_4_co), .A(A[4]), .B(B[4]), .S1(S1), .S0(S0), .F(F[4]), .Co(n1bit_au_5_co));
  _1bit_AU u_1bit_au_6 (.Ci(n1bit_au_5_co), .A(A[5]), .B(B[5]), .S1(S1), .S0(S0), .F(F[5]), .Co(n1bit_au_6_co));
  _1bit_AU u_1bit_au_7 (.Ci(n1bit_au_6_co), .A(A[6]), .B(B[6]), .S1(S1), .S0(S0), .F(F[6]), .Co(n1bit_au_7_co));
  _1bit_AU u_1bit_au_8 (.Ci(n1bit_au_7_co), .A(A[7]), .B(B[7]), .S1(S1), .S0(S0), .F(F[7]), .Co(Co));
  xor xor_1 (V, n1bit_au_7_co, Co);
endmodule

module _8bit_ALU (
  input  Ci,
  input  [7:0] A,
  input  [7:0] B,
  input  S2,
  input  H1,
  input  S1,
  input  H0,
  input  S0,
  output V,
  output Co,
  output Z,
  output S,
  output [7:0] F
);

  wire [7:0] n8bit_2x1_mux_1_o, n8bit_au_1_f, n8bit_lu_1_f;

  _8bit_AU u_8bit_au_1 (.Ci(Ci), .A(A), .B(B), .S1(S1), .S0(S0), .F(n8bit_au_1_f), .V(V), .Co(Co));
  _8bit_LU u_8bit_lu_1 (.A(A), .B(B), .S1(S1), .S0(S0), .F(n8bit_lu_1_f));
  _8bit_shifter u_8bit_shifter_1 (.SRin(1'b0), .SLin(1'b0), .O(F), .S1(H1), .S0(H0), .l(n8bit_2x1_mux_1_o));
  _8bit_2x1_MUX u_8bit_2x1_mux_1 (.A(n8bit_au_1_f), .B(n8bit_lu_1_f), .S(S2), .O(n8bit_2x1_mux_1_o));
  nor nor_1 (Z, F[0], F[1], F[2], F[3], F[4], F[5], F[6], F[7]);

  assign S = F[7];
endmodule

// 8 2x1
module _8bit_2x1_MUX (
  input  [7:0] A,
  input  [7:0] B,
  input  S,
  output [7:0] O
);

  _2x1_MUX u_2x1_mux_1 (.S(S), .l0(A[0]), .l1(B[0]), .O(O[0]));
  _2x1_MUX u_2x1_mux_2 (.S(S), .l0(A[1]), .l1(B[1]), .O(O[1]));
  _2x1_MUX u_2x1_mux_3 (.S(S), .l0(A[2]), .l1(B[2]), .O(O[2]));
  _2x1_MUX u_2x1_mux_4 (.S(S), .l0(A[3]), .l1(B[3]), .O(O[3]));
  _2x1_MUX u_2x1_mux_5 (.S(S), .l0(A[4]), .l1(B[4]), .O(O[4]));
  _2x1_MUX u_2x1_mux_6 (.S(S), .l0(A[5]), .l1(B[5]), .O(O[5]));
  _2x1_MUX u_2x1_mux_7 (.S(S), .l0(A[6]), .l1(B[6]), .O(O[6]));
  _2x1_MUX u_2x1_mux_8 (.S(S), .l0(A[7]), .l1(B[7]), .O(O[7]));
endmodule
