// Logisim project HW#05-4bit counter and decoder.circ as structural Verilog: 4 circuits, main circuit 4bit counter
module JK_flipflop (
  input  J,
  input  K,
  input  Ck,
  output Q,
  output nQ
);

  wire and_1_out, and_2_out, and_3_out, and_4_out, nand_1_out, nand_2_out, nor_1_out, nor_2_out, not_1_out;

  nand nand_1 (nand_1_out, Q, K);
  not not_1 (not_1_out, Ck);
  nand nand_2 (nand_2_out, J, nQ);
  and and_1 (and_1_out, nand_1_out, J, not_1_out);
  and and_2 (and_2_out, not_1_out, K, nand_2_out);
  nor nor_1 (nor_1_out, and_1_out, nor_2_out);
  nor nor_2 (nor_2_out, nor_1_out, and_2_out);
  and and_3 (and_3_out, nor_1_out, Ck);
  and and_4 (and_4_out, Ck, nor_2_out);
  nor nor_3 (Q, and_3_out, nQ);
  nor nor_4 (nQ, Q, and_4_out);
endmodule

module _4bit_counter (
  output [3:0] F
);

  wire and_1_out, and_2_out, Ck_out;

  Clock Ck (.out(Ck_out));
  T_Flip_Flop t_ff_1 (.clk(Ck_out), .T(and_1_out), .Q(F[3]), .en(1'b1));  // open: Qn, preset, reset
  and and_1 (and_1_out, F[2], and_2_out);
  and and_2 (and_2_out, F[0], F[1]);
  T_Flip_Flop t_ff_2 (.clk(Ck_out), .T(and_2_out), .Q(F[2]), .en(1'b1));  // open: Qn, preset, reset
  T_Flip_Flop t_ff_3 (.clk(Ck_out), .T(F[0]), .Q(F[1]), .en(1'b1));  // open: Qn, preset, reset
  T_Flip_Flop t_ff_4 (.clk(Ck_out), .T(1'b1), .Q(F[0]), .en(1'b1));  // open: Qn, preset, reset
endmodule

// 3x8
module _3x8_Decoder (
  input  C2,
  input  C1,
  input  C0,
  input  E,
  output D0,
  output D1,
  output D2,
  output D3,
  output D4,
  output D5,
  output D6,
  output D7
);

  wire not_1_out, not_2_out, not_3_out;

  not not_1 (not_1_out, C2);
  not not_2 (not_2_out, C1);
  not not_3 (not_3_out, C0);
  and and_1 (D0, not_1_out, not_2_out, not_3_out, E);
  and and_2 (D1, not_1_out, not_2_out, C0, E);
  and and_3 (D2, not_1_out, C1, not_3_out, E);
  and and_4 (D3, not_1_out, C1, C0, E);
  and and_5 (D4, C2, not_2_out, not_3_out, E);
  and and_6 (D5, C2, not_2_out, C0, E);
  and and_7 (D6, C2, C1, not_3_out, E);
  and and_8 (D7, C2, C1, C0, E);
endmodule

module _4x16_Decoder (
  input  C3,
  input  C2,
  input  C1,
  input  C0,
  output [15:0] out_5
);

  wire not_1_out;

  not not_1 (not_1_out, C3);
  _3x8_Decoder u_3x8_decoder_1 (
    .C2(C2), .C1(C1), .C0(C0), .E(not_1_out), .D0(out_5[0]), .D1(out_5[1]), .D2(out_5[2]), .D3(out_5[3]),
    .D4(out_5[4]), .D5(out_5[5]), .D6(out_5[6]), .D7(out_5[7]));
  _3x8_Decoder u_3x8_decoder_2 (
    .C2(C2), .C1(C1), .C0(C0), .E(C3), .D0(out_5[8]), .D1(out_5[9]), .D2(out_5[10]), .D3(out_5[11]),
    .D4(out_5[12]), .D5(out_5[13]), .D6(out_5[14]), .D7(out_5[15]));
endmodule
