// Logisim project HW#06-CPU Control bits.circ as structural Verilog: 2 circuits, main circuit main
module main (
  input  acld,
  input  [1:0] A,
  input  pcld,
  input  [5:0] ALU,
  input  [1:0] B,
  input  iraddrld,
  input  mbrld,
  input  M,
  input  marld,
  input  iropld,
  input  in_11,
  input  rw,
  input  in_13
);

  wire clock_1_out, not_1_out;
  wire [7:0] AC_q, controlled_buffer_1_out, IR_Addr_q, MAR_q, MBR_q, multiplexer_1_out, multiplexer_2_out,
       multiplexer_3_out, n8bit_alu_1_f, PC_q;

  Multiplexer #(.width(8)) multiplexer_1 (
    .in0(n8bit_alu_1_f), .in1(controlled_buffer_1_out), .out(multiplexer_1_out), .sel(M));  // open: en
  Register AC (.D(n8bit_alu_1_f), .en(acld), .Q(AC_q), .clk(clock_1_out), .clr(in_11));
  Register PC (.D(n8bit_alu_1_f), .en(pcld), .Q(PC_q), .clk(clock_1_out), .clr(in_11));
  Register IR_Addr (.D(n8bit_alu_1_f), .en(iraddrld), .Q(IR_Addr_q), .clk(clock_1_out), .clr(in_11));
  Register MBR (.D(multiplexer_1_out), .en(mbrld), .Q(MBR_q), .clk(clock_1_out), .clr(in_11));
  Register MAR (.D(n8bit_alu_1_f), .en(marld), .Q(MAR_q), .clk(clock_1_out), .clr(in_11));
  Clock clock_1 (.out(clock_1_out));
  assign controlled_buffer_1_out = not_1_out ? MBR_q : 8'bz;  // Controlled_Buffer controlled_buffer_1
  not not_1 (not_1_out, rw);
  Multiplexer #(.select(2), .width(8)) multiplexer_2 (
    .in0(AC_q), .in1(PC_q), .in2(IR_Addr_q), .in3(MBR_q), .out(multiplexer_2_out), .sel(A));  // open: en
  // Probe on multiplexer_2_out
  // Probe on multiplexer_3_out
  Multiplexer #(.select(2), .width(8)) multiplexer_3 (
    .in0(AC_q), .in1(PC_q), .in2(IR_Addr_q), .in3(MBR_q), .out(multiplexer_3_out), .sel(B));  // open: en
  Register IR_Op (.D(MBR_q), .en(iropld), .clk(clock_1_out), .clr(in_11));  // open: Q
  // Probe on n8bit_alu_1_f
  _8bit_ALU u_8bit_alu_1 (
    .A(multiplexer_2_out), .B(multiplexer_3_out), .in_3(ALU), .F(n8bit_alu_1_f));  // open: V, Co, Z, S
  RAM ram_1 (.addr(MAR_q), .data(controlled_buffer_1_out), .sel(in_13), .clk(clock_1_out), .ld(rw));  // open: clr
endmodule

module _8bit_ALU (
  input  [7:0] A,
  input  [7:0] B,
  input  [5:0] in_3,
  output V,
  output Co,
  output Z,
  output S,
  output [7:0] F
);

  wire n8bit_2x1_mux_1_p3, n8bit_au_1_p7, n8bit_lu_1_p5;

  // _8bit_AU 8bit_au_1: pin names not known; wires that end beside it: A, B, in_3[4], in_3[3], in_3[2], Co, n8bit_au_1_p7, V
  // _8bit_LU 8bit_lu_1: pin names not known; wires that end beside it: A, B, in_3[4], in_3[3], n8bit_lu_1_p5, n8bit_lu_1_p5
  // _8bit_2x1_MUX 8bit_2x1_mux_1: pin names not known; wires that end beside it: n8bit_au_1_p7, in_3[5], n8bit_2x1_mux_1_p3, 1'b0, n8bit_2x1_mux_1_p3, 1'b0
  // _8bit_shifter 8bit_shifter_1: pin names not known; wires that end beside it: in_3[1], in_3[0], F
  nor nor_1 (Z, F[0], F[1], F[2], F[3], F[4], F[5], F[6], F[7]);

  assign S = F[7];
endmodule
