// Logisim project HW#07-ISA.circ as structural Verilog: 3 circuits, main circuit main
module main (
  input  rst,
  input  in_2
);

  wire acld, clock_1_out, IRaddrld, IRopld, M, marld, mbrld, not_1_out, pcld, rw, stld;
  wire [1:0] A, B;
  wire [2:0] control_unit_1_cnt;
  wire [3:0] n8bit_alu_1_v, status_q;
  wire [5:0] ALU;
  wire [7:0] AC_q, controlled_buffer_1_out, IR_Addr_q, IR_Op_q, MAR_q, MBR_q, multiplexer_1_out,
       multiplexer_2_out, multiplexer_3_out, n8bit_alu_1_f, PC_q;

  Multiplexer #(.width(8)) multiplexer_1 (
    .in0(n8bit_alu_1_f), .in1(controlled_buffer_1_out), .out(multiplexer_1_out), .sel(M));  // open: en
  Register AC (.D(n8bit_alu_1_f), .en(acld), .Q(AC_q), .clk(clock_1_out), .clr(rst));
  Register PC (.D(n8bit_alu_1_f), .en(pcld), .Q(PC_q), .clk(clock_1_out), .clr(rst));
  Register IR_Addr (.D(n8bit_alu_1_f), .en(IRaddrld), .Q(IR_Addr_q), .clk(clock_1_out), .clr(rst));
  Register MBR (.D(multiplexer_1_out), .en(mbrld), .Q(MBR_q), .clk(clock_1_out), .clr(rst));
  Register MAR (.D(n8bit_alu_1_f), .en(marld), .Q(MAR_q), .clk(clock_1_out), .clr(rst));
  Clock clock_1 (.out(clock_1_out));
  assign controlled_buffer_1_out = not_1_out ? MBR_q : 8'bz;  // Controlled_Buffer controlled_buffer_1
  not not_1 (not_1_out, rw);
  Multiplexer #(.select(2), .width(8)) multiplexer_2 (
    .in0(AC_q), .in1(PC_q), .in2(IR_Addr_q), .in3(MBR_q), .out(multiplexer_2_out), .sel(A));  // open: en
  // Probe on multiplexer_2_out
  // Probe on multiplexer_3_out
  // Probe on ALU
  Multiplexer #(.select(2), .width(8)) multiplexer_3 (
    .in0(AC_q), .in1(PC_q), .in2(IR_Addr_q), .in3(MBR_q), .out(multiplexer_3_out), .sel(B));  // open: en
  Register #(.width(4)) status (.D(n8bit_alu_1_v), .en(stld), .Q(status_q), .clk(clock_1_out), .clr(rst));
  Register IR_Op (.D(MBR_q), .en(IRopld), .Q(IR_Op_q), .clk(clock_1_out), .clr(rst));
  // Probe on n8bit_alu_1_f
  _8bit_ALU u_8bit_alu_1 (
    .A(multiplexer_2_out), .B(multiplexer_3_out), .in_3(ALU), .V(n8bit_alu_1_v[0]), .Co(n8bit_alu_1_v[1]),
    .Z(n8bit_alu_1_v[2]), .S(n8bit_alu_1_v[3]), .F(n8bit_alu_1_f));
  // Probe on control_unit_1_cnt
  Control_Unit control_unit_1 (
    .Ck(clock_1_out), .RST(rst), .status(status_q), .IR_Op(IR_Op_q),
    .LDs({stld, IRopld, marld, mbrld, IRaddrld, pcld, acld}), .cnt(control_unit_1_cnt), .ALU(ALU), .M(M),
    .A(A), .B(B), .rw(rw));
  // Probe on A
  // Probe on B
  RAM ram_1 (.addr(MAR_q), .data(controlled_buffer_1_out), .sel(in_2), .clk(clock_1_out), .ld(rw));  // open: clr
endmodule

module _8bit_ALU (
  input  [7:0] A,
  input  [7:0] B,
  input  [5:0] in_3,
  output V,
  output Co,
  output Z,
  output S,
  output [7:0] F
);

  wire n8bit_2x1_mux_1_p3, n8bit_au_1_p6, n8bit_lu_1_p6;

  // _8bit_AU 8bit_au_1: pin names not known; wires that end beside it: A, B, in_3[4], in_3[3], in_3[2], n8bit_au_1_p6, V
  // _8bit_LU 8bit_lu_1: pin names not known; wires that end beside it: A, B, in_3[4], in_3[3], Co, n8bit_lu_1_p6, n8bit_lu_1_p6
  // _8bit_shifter 8bit_shifter_1: pin names not known; wires that end beside it: in_3[1], in_3[0], F
  // _8bit_2x1_MUX 8bit_2x1_mux_1: pin names not known; wires that end beside it: n8bit_au_1_p6, in_3[5], n8bit_2x1_mux_1_p3, 1'b0, n8bit_2x1_mux_1_p3, 1'b0
  nor nor_1 (Z, F[0], F[1], F[2], F[3], F[4], F[5], F[6], F[7]);

  assign S = F[7];
endmodule

// CU
module Control_Unit (
  input  Ck,
  input  RST,
  input  [3:0] status,
  input  [7:0] IR_Op,
  output [6:0] LDs,
  output [2:0] cnt,
  output [5:0] ALU,
  output M,
  output [1:0] A,
  output [1:0] B,
  output rw
);

  wire ADD, AND, BZ, JMP, LDA, NOP, NOT, not_1_out, OR, SHL, SHR, STR, SUB, T0, T1, T4, T5, T6, T7, XOR;

  Counter #(.width(3), .max('h7)) counter_1 (.Q(cnt), .clk(not_1_out), .clr(RST));  // open: load, D, count, carry
  not not_1 (not_1_out, Ck);
  Decoder #(.select(3), .disabled(0), .enable("false")) decoder_1 (
    .out0(T0), .out1(T1), .out2(LDs[1]), .out3(A[1]), .out4(T4), .out5(T5), .out6(T6), .out7(T7), .sel(cnt));
  Decoder #(.select(4), .disabled(0), .enable("false")) decoder_2 (
    .out0(NOP), .out1(NOT), .out2(SHL), .out3(SHR), .out4(JMP), .out5(BZ), .out8(LDA), .out9(ADD),
    .out10(SUB), .out11(AND), .out12(OR), .out13(XOR), .out15(STR), .sel(IR_Op[7:4]));  // open: out6, out7, out14
  or or_1 (LDs[2], T0, T1);
  or or_2 (ALU[2], T1, LDs[1]);

  assign A[0] = 1'b1;
  assign {ALU[5:3], ALU[1:0]} = {5{1'b0}};
  assign B = 2'b11;
  assign {LDs[6:3], LDs[0]} = {1'b0, ALU[2], A[1], ALU[2], 1'b0};
  assign M = ALU[2];
  assign rw = 1'b1;

  // Other names for the same wires on the sheet: T3 = A[1]; T2 = LDs[1]; V = status[0]; C = status[1]; Z = status[2];
  //   S = status[3]
endmodule
