// Logisim project HW#LAST-8bitCPU.circ as structural Verilog: 3 circuits, main circuit main
module main (
  input  rst,
  input  in_2
);

  wire acld, clock_1_out, IRaddrld, IRopld, M, marld, mbrld, not_1_out, pcld, rw, stld;
  wire [1:0] A, B;
  wire [2:0] control_unit_1_cnt;
  wire [3:0] n8bit_alu_1_v, status_q;
  wire [5:0] ALU;
  wire [7:0] AC_q, controlled_buffer_1_out, IR_Addr_q, IR_Op_q, MAR_q, MBR_q, multiplexer_1_out,
       multiplexer_2_out, multiplexer_3_out, n8bit_alu_1_f, PC_q;

  Multiplexer #(.width(8), .enable("false")) multiplexer_1 (
    .in0(n8bit_alu_1_f), .in1(controlled_buffer_1_out), .out(multiplexer_1_out), .sel(M));
  Register AC (.D(n8bit_alu_1_f), .en(acld), .Q(AC_q), .clk(clock_1_out), .clr(rst));
  Register PC (.D(n8bit_alu_1_f), .en(pcld), .Q(PC_q), .clk(clock_1_out), .clr(rst));
  Register IR_Addr (.D(n8bit_alu_1_f), .en(IRaddrld), .Q(IR_Addr_q), .clk(clock_1_out), .clr(rst));
  Register MBR (.D(multiplexer_1_out), .en(mbrld), .Q(MBR_q), .clk(clock_1_out), .clr(rst));
  Register MAR (.D(n8bit_alu_1_f), .en(marld), .Q(MAR_q), .clk(clock_1_out), .clr(rst));
  Clock clock_1 (.out(clock_1_out));
  assign controlled_buffer_1_out = not_1_out ? MBR_q : 8'bz;  // Controlled_Buffer controlled_buffer_1
  not not_1 (not_1_out, rw);
  Multiplexer #(.select(2), .width(8), .enable("false")) multiplexer_2 (
    .in0(AC_q), .in1(PC_q), .in2(IR_Addr_q), .in3(MBR_q), .out(multiplexer_2_out), .sel(A));
  // Probe on multiplexer_2_out
  // Probe on multiplexer_3_out
  // Probe on ALU
  Multiplexer #(.select(2), .width(8), .enable("false")) multiplexer_3 (
    .in0(AC_q), .in1(PC_q), .in2(IR_Addr_q), .in3(MBR_q), .out(multiplexer_3_out), .sel(B));
  Register #(.width(4)) status (.D(n8bit_alu_1_v), .en(stld), .Q(status_q), .clk(clock_1_out), .clr(rst));
  Register IR_Op (.D(MBR_q), .en(IRopld), .Q(IR_Op_q), .clk(clock_1_out), .clr(rst));
  // Probe on n8bit_alu_1_f
  // Probe on n8bit_alu_1_v
  _8bit_ALU u_8bit_alu_1 (
    .A(multiplexer_2_out), .B(multiplexer_3_out), .in_3(ALU), .V(n8bit_alu_1_v[0]), .Co(n8bit_alu_1_v[1]),
    .Z(n8bit_alu_1_v[2]), .S(n8bit_alu_1_v[3]), .F(n8bit_alu_1_f));
  // Probe on control_unit_1_cnt
  Control_Unit control_unit_1 (
    .Ck(clock_1_out), .RST(rst), .status(status_q), .IR_Op(IR_Op_q),
    .LDs({acld, pcld, IRaddrld, mbrld, marld, IRopld, stld}), .cnt(control_unit_1_cnt), .ALU(ALU), .M(M),
    .A(A), .B(B), .rw(rw));
  // Probe on A
  // Probe on B
  RAM ram_1 (.addr(MAR_q), .data(controlled_buffer_1_out), .sel(in_2), .clk(clock_1_out), .ld(rw));  // open: clr
endmodule

module _8bit_ALU (
  input  [7:0] A,
  input  [7:0] B,
  input  [5:0] in_3,
  output V,
  output Co,
  output Z,
  output S,
  output [7:0] F
);

  wire n8bit_2x1_mux_1_p3, n8bit_au_1_p6, n8bit_lu_1_p6;

  // _8bit_AU 8bit_au_1: pin names not known; wires that end beside it: A, B, in_3[4], in_3[3], in_3[2], n8bit_au_1_p6, V
  // _8bit_LU 8bit_lu_1: pin names not known; wires that end beside it: A, B, in_3[4], in_3[3], Co, n8bit_lu_1_p6, n8bit_lu_1_p6
  // _8bit_2x1_MUX 8bit_2x1_mux_1: pin names not known; wires that end beside it: n8bit_au_1_p6, in_3[5], n8bit_2x1_mux_1_p3, 1'b0, n8bit_2x1_mux_1_p3, 1'b0
  // _8bit_shifter 8bit_shifter_1: pin names not known; wires that end beside it: in_3[1], in_3[0], F
  nor nor_1 (Z, F[0], F[1], F[2], F[3], F[4], F[5], F[6], F[7]);

  assign S = F[7];
endmodule

// CU
module Control_Unit (
  input  RST,
  input  Ck,
  input  [3:0] status,
  input  [7:0] IR_Op,
  output [2:0] cnt,
  output [6:0] LDs,
  output [5:0] ALU,
  output [1:0] A,
  output [1:0] B,
  output M,
  output rw
);

  wire AC2BR, ADD, ADD_T4, ADD_T5, ADD_T6, ADD_T7, AND, and_25_out, and_26_out, AND_T4, AND_T5, AND_T6,
       AND_T7, BNZ, BNZ_T4, BNZ_T5, BR2AC, BZ, BZ_T4, BZ_T5, IRAD2AR, IRAD2PC, JMP, JMP_T4, JMP_T5, LDA,
       LDA_T4, LDA_T5, LDA_T7, NOP, NOT, not_1_out, not_2_out, NOT_T4, NOT_T5, OR, or_1_out, OR_T4, OR_T5,
       OR_T6, OR_T7, READ, SHL, SHL_T5, SHR, SHR_T5, STR, STR_T4, STR_T6, STR_T7, SUB, SUB_T4, SUB_T5,
       SUB_T6, SUB_T7, T0, T1, T4, T5, T6, T7, uXOR, XOR, XOR_T4, XOR_T5, XOR_T7;

  and and_1 (NOT_T4, NOT, T4);
  and and_2 (NOT_T5, NOT, T5);
  and and_3 (ALU[1], SHL, T4);
  and and_4 (SHL_T5, SHL, T5);
  and and_5 (ALU[0], SHR, T4);
  and and_6 (SHR_T5, SHR, T5);
  and and_7 (JMP_T4, JMP, T4);
  and and_8 (JMP_T5, JMP, T5);
  and and_9 (BZ_T4, BZ, T4);
  and and_10 (BZ_T5, BZ, T5);
  and and_11 (BNZ_T4, BNZ, T4);
  and and_12 (BNZ_T5, BNZ, T5);
  and and_13 (LDA_T4, LDA, T4);
  and and_14 (LDA_T5, LDA, T5);
  and and_15 (BR2AC, LDA, T6);
  and and_16 (LDA_T7, LDA, T7);
  and and_17 (SUB_T4, SUB, T4);
  and and_18 (SUB_T5, SUB, T5);
  and and_19 (SUB_T6, SUB, T6);
  and and_20 (SUB_T7, SUB, T7);
  Counter #(.width(3), .max('h7)) counter_1 (.Q(cnt), .clk(not_1_out), .clr(or_1_out));  // open: load, D, count, carry
  not not_1 (not_1_out, Ck);
  or or_1 (or_1_out, RST, XOR_T7, NOT_T5, LDA_T7, SHL_T5, OR_T7, SHR_T5, SUB_T7, JMP_T5, ADD_T7, BZ_T5, STR_T7, BNZ_T5, AND_T7);
  Decoder #(.select(4), .disabled(0), .enable("false")) decoder_1 (
    .out0(NOP), .out1(NOT), .out2(SHL), .out3(SHR), .out4(JMP), .out5(BZ), .out6(BNZ), .out8(LDA),
    .out9(ADD), .out10(SUB), .out11(AND), .out12(OR), .out13(XOR), .out15(STR), .sel(IR_Op[7:4]));  // open: out7, out14
  and and_21 (AND_T4, AND, T4);
  and and_22 (AND_T5, AND, T5);
  and and_23 (AND_T6, AND, T6);
  and and_24 (AND_T7, AND, T7);
  Decoder #(.select(3), .disabled(0), .enable("false")) decoder_2 (
    .out0(T0), .out1(T1), .out2(LDs[1]), .out3(LDs[4]), .out4(T4), .out5(T5), .out6(T6), .out7(T7), .sel(cnt));
  or or_2 (IRAD2AR, LDA_T4, ADD_T4, SUB_T4, AND_T4, OR_T4, XOR_T4, STR_T4);
  and and_25 (and_25_out, BNZ_T4, not_2_out);
  not not_2 (not_2_out, status[2]);
  and and_26 (and_26_out, BZ_T4, status[2]);
  and and_27 (ADD_T4, ADD, T4);
  and and_28 (ADD_T5, ADD, T5);
  and and_29 (ADD_T6, ADD, T6);
  and and_30 (ADD_T7, ADD, T7);
  or or_3 (READ, ADD_T5, LDA_T5, SUB_T5, AND_T5, OR_T5, XOR_T5);
  or or_4 (IRAD2PC, and_25_out, JMP_T4, and_26_out);
  and and_31 (OR_T4, OR, T4);
  and and_32 (OR_T5, OR, T5);
  and and_33 (OR_T6, OR, T6);
  and and_34 (OR_T7, OR, T7);
  or or_5 (LDs[2], T0, IRAD2AR, T1);
  or or_6 (LDs[3], T1, READ, AC2BR, LDs[1]);
  or or_7 (ALU[2], T1, SUB_T6, LDs[1]);
  or or_8 (ALU[3], ADD_T6, OR_T6, NOT_T4);
  or or_9 (ALU[4], NOT_T4, SUB_T6, uXOR);
  or or_10 (ALU[5], NOT_T4, AND_T6, OR_T6, uXOR);
  and and_35 (XOR_T4, XOR, T4);
  and and_36 (XOR_T5, XOR, T5);
  and and_37 (uXOR, XOR, T6);
  and and_38 (XOR_T7, XOR, T7);
  or or_11 (LDs[0], NOT_T4, SUB_T6, AND_T6, BR2AC, OR_T6, ADD_T6, uXOR, ALU[1], ALU[0]);
  or or_12 (LDs[5], T1, IRAD2PC, LDs[1]);
  or or_13 (LDs[6], SUB_T6, OR_T6, uXOR, ADD_T6, BR2AC, AND_T6);
  or or_14 (A[0], T0, T1, LDs[1], LDs[4], BR2AC);
  or or_15 (A[1], LDs[4], IRAD2AR, IRAD2PC, BR2AC);
  or or_16 (B[1], ADD_T6, SUB_T6, AND_T6, OR_T6, uXOR);
  or or_17 (M, T1, READ, LDs[1]);
  not not_3 (rw, STR_T6);
  and and_39 (STR_T4, STR, T4);
  and and_40 (AC2BR, STR, T5);
  and and_41 (STR_T6, STR, T6);
  and and_42 (STR_T7, STR, T7);

  assign B[0] = B[1];

  // Other names for the same wires on the sheet: SHR_T4 = ALU[0]; uSHR = ALU[0]; SHL_T4 = ALU[1]; uSHL = ALU[1];
  //   LDA_T6 = BR2AC; T2 = LDs[1]; T3 = LDs[4]; V = status[0]; C = status[1]; Z = status[2]; S = status[3];
  //   STR_T5 = AC2BR; uADD = ADD_T6; uAND = AND_T6; uNOT = NOT_T4; uOR = OR_T6; uSUB = SUB_T6; XOR_T6 = uXOR;
  //   WRITE = STR_T6
endmodule
